// Logisim project ex2.circ as structural Verilog: 1 circuit, main circuit AddMachine
module AddMachine (
  output [7:0] ADD_OUT,
  output [7:0] REG_OUT
);

  wire Clock0_out;

  Register Register0 (.D(ADD_OUT), .clk(Clock0_out), .Q(REG_OUT));  // open: en, clr
  Clock Clock0 (.out(Clock0_out));
  Adder adder_1 (.a(REG_OUT), .b(8'h1), .out(ADD_OUT));  // open: cin, cout

  // Notes on the sheet:
  //   PUT CIRCUITRY HERE
endmodule
