// Logisim project ex1.circ as structural Verilog: 4 circuits, main circuit main
module main (
  output [7:0] non_pipe_out,
  output [7:0] pipe_out
);

  wire CLK_out;
  wire [7:0] Address_Counter_q, rom_1_data;

  Counter Address_Counter (.clk(CLK_out), .Q(Address_Counter_q));  // open: clr, load, up, count, D, carry
  Clock CLK (.out(CLK_out));
  ROM rom_1 (.addr(Address_Counter_q), .data(rom_1_data));
  // Probe on non_pipe_out
  non_pipelined non_pipelined_1 (.in1(rom_1_data[3:0]), .in2(rom_1_data[7:4]), .CLK(CLK_out), .out1(non_pipe_out));
  // Probe on pipe_out
  pipelined pipelined_1 (.in1(rom_1_data[3:0]), .in2(rom_1_data[7:4]), .CLK(CLK_out), .out1(pipe_out));

  // Notes on the sheet:
  //   contents of rom_1 (hex, n*v repeats v):
  //   13 a2 fc 8f 1c 2 b0
endmodule

module non_pipelined (
  input  [3:0] in1,
  input  [3:0] in2,
  input  CLK,
  output [7:0] out1
);

  wire [7:0] move_and_add_1_moved_multiplicand, move_and_add_1_result, move_and_add_2_moved_multiplicand,
       move_and_add_2_result, move_and_add_3_moved_multiplicand, move_and_add_3_result, move_and_add_4_result;

  // Probe on move_and_add_1_result
  move_and_add move_and_add_1 (
    .multiplicand({4'b0000, in1}), .result(move_and_add_1_result), .current({8{1'b0}}), .multiplier(in2[0]),
    .moved_multiplicand(move_and_add_1_moved_multiplicand));
  move_and_add move_and_add_2 (
    .multiplicand(move_and_add_1_moved_multiplicand), .result(move_and_add_2_result),
    .current(move_and_add_1_result), .multiplier(in2[1]),
    .moved_multiplicand(move_and_add_2_moved_multiplicand));
  move_and_add move_and_add_3 (
    .multiplicand(move_and_add_2_moved_multiplicand), .result(move_and_add_3_result),
    .current(move_and_add_2_result), .multiplier(in2[2]),
    .moved_multiplicand(move_and_add_3_moved_multiplicand));
  move_and_add move_and_add_4 (
    .multiplicand(move_and_add_3_moved_multiplicand), .result(move_and_add_4_result),
    .current(move_and_add_3_result), .multiplier(in2[3]));  // open: moved_multiplicand
  Register register_1 (.D(move_and_add_4_result), .clk(CLK), .Q(out1));  // open: en, clr
endmodule

module pipelined (
  input  [3:0] in1,
  input  [3:0] in2,
  input  CLK,
  output [7:0] out1
);

  wire register_3_q, register_4_q;
  wire [7:0] move_and_add_1_moved_multiplicand, move_and_add_1_result, move_and_add_2_moved_multiplicand,
       move_and_add_2_result, move_and_add_3_moved_multiplicand, move_and_add_3_result,
       move_and_add_4_result, register_1_q, register_2_q;

  // Probe on move_and_add_1_result
  move_and_add move_and_add_1 (
    .multiplicand({4'b0000, in1}), .result(move_and_add_1_result), .current({8{1'b0}}), .multiplier(in2[0]),
    .moved_multiplicand(move_and_add_1_moved_multiplicand));
  Register register_1 (.D(move_and_add_2_result), .clk(CLK), .Q(register_1_q));  // open: en, clr
  move_and_add move_and_add_2 (
    .multiplicand(move_and_add_1_moved_multiplicand), .result(move_and_add_2_result),
    .current(move_and_add_1_result), .multiplier(in2[1]),
    .moved_multiplicand(move_and_add_2_moved_multiplicand));
  Register register_2 (.D(move_and_add_2_moved_multiplicand), .clk(CLK), .Q(register_2_q));  // open: en, clr
  Register #(.width(1)) register_3 (.D(in2[2]), .clk(CLK), .Q(register_3_q));  // open: en, clr
  Register #(.width(1)) register_4 (.D(in2[3]), .clk(CLK), .Q(register_4_q));  // open: en, clr
  move_and_add move_and_add_3 (
    .multiplicand(register_2_q), .result(move_and_add_3_result), .current(register_1_q),
    .multiplier(register_3_q), .moved_multiplicand(move_and_add_3_moved_multiplicand));
  move_and_add move_and_add_4 (
    .multiplicand(move_and_add_3_moved_multiplicand), .result(move_and_add_4_result),
    .current(move_and_add_3_result), .multiplier(register_4_q));  // open: moved_multiplicand
  Register register_5 (.D(move_and_add_4_result), .clk(CLK), .Q(out1));  // open: en, clr
endmodule

module move_and_add (
  input  [7:0] current,
  input  [7:0] multiplicand,
  input  multiplier,
  output [7:0] result,
  output [7:0] moved_multiplicand
);

  wire [7:0] multiplexer_1_out;

  Multiplexer #(.width(8), .enable("false")) multiplexer_1 (
    .in0({8{1'b0}}), .in1(multiplicand), .out(multiplexer_1_out), .sel(multiplier));
  Adder adder_1 (.a(current), .b(multiplexer_1_out), .out(result));  // open: cin, cout
  Shifter shifter_1 (.in(multiplicand), .\dist (3'b001), .out(moved_multiplicand));
endmodule
